// Logisim project All_7_Gates.circ as structural Verilog: 7 circuits, main circuit AND
module AND (
  input  A,
  input  B,
  output Y
);

  and and_1 (Y, A, B);
endmodule

module OR (
  input  A,
  input  B,
  output Y
);

  or or_1 (Y, A, B);
endmodule

module NAND (
  input  A,
  input  B,
  output Y
);

  // NAND_Gate nand_1 has open pins: out=Y
endmodule

module NOR (
  input  A,
  input  B,
  output Y
);

  // NOR_Gate nor_1 has open pins: out=Y
endmodule

module XOR (
  input  A,
  input  B,
  output Y
);

  // XOR_Gate xor_1 has open pins: out=Y
endmodule

module XNOR (
  input  A,
  input  B,
  output Y
);

  // XNOR_Gate xnor_1 has open pins: out=Y
endmodule

module NOT (
  input  A,
  output Y
);

  not not_1 (Y, A);
endmodule
