// Logisim project Half_Full_Adder.circ as structural Verilog: 4 circuits, main circuit Half_Adder
module Half_Adder (
  input  A,
  input  B,
  output Sum,
  output Carry
);

  // XOR_Gate xor_1 has open pins: out=Sum
  and and_1 (Carry, A, B);
endmodule

module Half_Adder_NAND (
  input  A,
  input  B,
  output Sum,
  output Carry
);

  wire nand_1_out, nand_2_out, nand_3_out;

  // NAND_Gate nand_1 has open pins: out=nand_1_out
  // NAND_Gate nand_2 has open pins: out=nand_2_out
  // NAND_Gate nand_3 has open pins: out=nand_3_out
  // NAND_Gate nand_4 has open pins: out=Sum
  // NAND_Gate nand_5 has open pins: out=Carry
endmodule

module Full_Adder (
  input  A,
  input  B,
  input  Cin,
  output Sum,
  output Cout
);

  wire and_1_out, and_2_out, xor_1_out;

  // XOR_Gate xor_1 has open pins: out=xor_1_out
  // XOR_Gate xor_2 has open pins: out=Sum
  and and_1 (and_1_out, xor_1_out, Cin);
  and and_2 (and_2_out, A, B);
  or or_1 (Cout, and_1_out, and_2_out);
endmodule

module Full_Adder_NAND (
  input  A,
  input  B,
  input  Cin,
  output Sum,
  output Carry
);

  wire nand_1_out, nand_2_out, nand_3_out, nand_4_out, nand_5_out, nand_6_out, nand_7_out;

  // NAND_Gate nand_1 has open pins: out=nand_1_out
  // NAND_Gate nand_2 has open pins: out=nand_2_out
  // NAND_Gate nand_3 has open pins: out=nand_3_out
  // NAND_Gate nand_4 has open pins: out=nand_4_out
  // NAND_Gate nand_5 has open pins: out=nand_5_out
  // NAND_Gate nand_6 has open pins: out=nand_6_out
  // NAND_Gate nand_7 has open pins: out=nand_7_out
  // NAND_Gate nand_8 has open pins: out=Sum
  // NAND_Gate nand_9 has open pins: out=Carry
endmodule
