// Logisim project Half_Full_Subtractor.circ as structural Verilog: 4 circuits, main circuit Half_Subtractor
module Half_Subtractor (
  input  A,
  input  B,
  output Difference,
  output Borrow
);

  wire not_1_out;

  not not_1 (not_1_out, A);
  // XOR_Gate xor_1 has open pins: out=Difference
  and and_1 (Borrow, not_1_out, B);
endmodule

module Half_Subtractor_NAND (
  input  A,
  input  B,
  output Difference,
  output Borrow
);

  wire nand_1_out, nand_2_out, nand_3_out;

  // NAND_Gate nand_1 has open pins: out=nand_1_out
  // NAND_Gate nand_2 has open pins: out=nand_2_out
  // NAND_Gate nand_3 has open pins: out=nand_3_out
  // NAND_Gate nand_4 has open pins: out=Difference
  // NAND_Gate nand_5 has open pins: out=Borrow
endmodule

module Full_Subtractor (
  input  A,
  input  B,
  input  Bin,
  output Difference,
  output Bout
);

  wire and_1_out, and_2_out, not_1_out, not_2_out, xor_1_out;

  // XOR_Gate xor_1 has open pins: out=xor_1_out
  not not_1 (not_1_out, xor_1_out);
  not not_2 (not_2_out, A);
  // XOR_Gate xor_2 has open pins: out=Difference
  and and_1 (and_1_out, not_1_out, Bin);
  and and_2 (and_2_out, not_2_out, B);
  or or_1 (Bout, and_1_out, and_2_out);
endmodule

module Full_Subtractor_NAND (
  input  A,
  input  B,
  input  Bin,
  output Difference,
  output Bout
);

  wire nand_1_out, nand_2_out, nand_3_out, nand_4_out, nand_5_out, nand_6_out, nand_7_out;

  // NAND_Gate nand_1 has open pins: out=nand_1_out
  // NAND_Gate nand_2 has open pins: out=nand_2_out
  // NAND_Gate nand_3 has open pins: out=nand_3_out
  // NAND_Gate nand_4 has open pins: out=nand_4_out
  // NAND_Gate nand_5 has open pins: out=nand_5_out
  // NAND_Gate nand_6 has open pins: out=nand_6_out
  // NAND_Gate nand_7 has open pins: out=nand_7_out
  // NAND_Gate nand_8 has open pins: out=Difference
  // NAND_Gate nand_9 has open pins: out=Bout
endmodule
