// Logisim project exp4.circ as structural Verilog: 4 circuits, main circuit Half_Subtractor
module Half_Subtractor (
  input  A,
  input  B,
  output Difference,
  output Borrow
);

  wire not_1_out;

  not not_1 (not_1_out, A);
  xor xor_1 (Difference, A, B);
  and and_1 (Borrow, not_1_out, B);
endmodule

module Half_Subtractor_NAND (
  input  A,
  input  B,
  output Difference,
  output Borrow
);

  wire nand_1_out, nand_2_out, nand_3_out;

  nand nand_1 (nand_1_out, A, B);
  nand nand_2 (nand_2_out, A, nand_1_out);
  nand nand_3 (nand_3_out, nand_1_out, B);
  nand nand_4 (Difference, nand_2_out, nand_3_out);
  nand nand_5 (Borrow, nand_3_out, nand_3_out);
endmodule

module Full_Subtractor (
  input  A,
  input  B,
  input  Bin,
  output Difference,
  output Bout
);

  wire and_1_out, and_2_out, not_1_out, not_2_out, xor_1_out;

  xor xor_1 (xor_1_out, A, B);
  not not_1 (not_1_out, A);
  and and_1 (and_1_out, not_1_out, B);
  not not_2 (not_2_out, xor_1_out);
  xor xor_2 (Difference, xor_1_out, Bin);
  and and_2 (and_2_out, not_2_out, Bin);
  or or_1 (Bout, and_1_out, and_2_out);
endmodule

module Full_Subtractor_NAND (
  input  A,
  input  B,
  input  Bin,
  output Difference,
  output Bout
);

  wire nand_1_out, nand_2_out, nand_3_out, nand_4_out, nand_5_out, nand_6_out, nand_7_out;

  nand nand_1 (nand_1_out, A, B);
  nand nand_2 (nand_2_out, A, nand_1_out);
  nand nand_3 (nand_3_out, nand_1_out, B);
  nand nand_4 (nand_4_out, nand_2_out, nand_3_out);
  nand nand_5 (nand_5_out, nand_4_out, Bin);
  nand nand_6 (nand_6_out, nand_4_out, nand_5_out);
  nand nand_7 (nand_7_out, nand_5_out, Bin);
  nand nand_8 (Difference, nand_6_out, nand_7_out);
  nand nand_9 (Bout, nand_3_out, nand_7_out);
endmodule
